# Fritzing sketch DIY_Security (saved by Fritzing 0.9.10b)
breadboards: 1

parts:
  Microwave_Sensor = DFRobot Microwave Sensor 5pin
  Mod1 = Raspberry Pi Pico W
  9V_Battery = BC9VPC [package=bc9vpc]
  R1 = Resistor [tolerance=±5% power=0.25 resistance=220 package=THT]
  R2 = Resistor [tolerance=±5% power=0.25 resistance=1.5k package=THT]
  R3 = Resistor [tolerance=±5% power=0.25 resistance=1k package=THT]
  LED1 = LED - 5mm [color="Red (633nm)" current=0.030 package="5 mm [THT]"]

nets:
  N1: Microwave_Sensor.RX, Mod1.pin_7
  N2: Microwave_Sensor.TX, Mod1.pin_6
  N3: Microwave_Sensor.OUT, Mod1.pin_5
  N4: Microwave_Sensor.GND, 9V_Battery.V-, R2.Pin_1, LED1.cathode
  N5: Microwave_Sensor.VCC, Mod1.pin_3, Mod1.pin_8, Mod1.pin_13, Mod1.pin_18, Mod1.pin_23, Mod1.pin_28, Mod1.pin_33, Mod1.pin_38, Mod1.pin_42, R2.Pin_0, R3.Pin_0
  N6: Mod1.pin_20, R1.Pin_0
  N7: Mod1.pin_39, 9V_Battery.V+, R3.Pin_1
  N8: R1.Pin_1, LED1.anode

custom parts:
  Raspberry Pi Pico W: Raspberry Pi Pico W. Based around the RP2040 microcontroller the Pico W is a low cost microcontroller device bringing Raspberry Pi quality, cost, and easy of use to the microcontroller space. The areas marked KEEPOUT in pcb silkscreen should not have traces running through them to avoid shorts on a soldered in module!
